# Fritzing sketch Arduino-Uno-Breadboard (saved by Fritzing 0.9.3b)
breadboards: 1

parts:
  Arduino_Uno = Arduino Uno (Rev3)
  R9 = Resistor [tolerance=±5% resistance=150 package=THT]
  R8 = Resistor [tolerance=±5% resistance=150 package=THT]
  R7 = Resistor [tolerance=±5% resistance=150 package=THT]
  R6 = Resistor [tolerance=±5% resistance=150 package=THT]
  R5 = Resistor [tolerance=±5% resistance=150 package=THT]
  R3 = Resistor [tolerance=±5% resistance=150 package=THT]
  R4 = Resistor [tolerance=±5% resistance=150 package=THT]
  R2 = Resistor [tolerance=±5% resistance=150 package=THT]
  LED9 = LED - 5mm [color="Red (633nm)" package="5 mm [THT]"]
  LED8 = LED - 5mm [color="Red (633nm)" package="5 mm [THT]"]
  LED7 = LED - 5mm [color="Red (633nm)" package="5 mm [THT]"]
  LED6 = LED - 5mm [color="Red (633nm)" package="5 mm [THT]"]
  LED5 = LED - 5mm [color="Green (555nm)" package="5 mm [THT]"]
  LED4 = LED - 5mm [color="Green (555nm)" package="5 mm [THT]"]
  LED3 = LED - 5mm [color="Green (555nm)" package="5 mm [THT]"]
  LED2 = LED - 5mm [color="Green (555nm)" package="5 mm [THT]"]
  R1 = Resistor [tolerance=±5% resistance=150 package=THT]
  LED1 = LED - 5mm [color="Green (555nm)" package="5 mm [THT]"]
  LED0 = LED - 5mm [color="Blue (430nm)" package="5 mm [THT]"]
  R0 = Resistor [tolerance=±5% resistance=150 package=THT]

nets:
  N1: Arduino_Uno.D8, LED5.anode
  N2: Arduino_Uno.D9_PWM, LED6.anode
  N3: Arduino_Uno.D10_PWM/SS, LED7.anode
  N4: Arduino_Uno.D11_PWM/MOSI, LED8.anode
  N5: Arduino_Uno.D12/MISO, LED9.anode
  N6: Arduino_Uno.GND, R9.Pin_1, R8.Pin_1, R7.Pin_1, R6.Pin_1, R5.Pin_1, R3.Pin_1, R4.Pin_1, R2.Pin_1, R1.Pin_1, R0.Pin_1
  N7: Arduino_Uno.D3_PWM, LED0.anode
  N8: Arduino_Uno.D4, LED1.anode
  N9: Arduino_Uno.D5_PWM, LED2.anode
  N10: Arduino_Uno.D6_PWM, LED3.anode
  N11: Arduino_Uno.D7, LED4.anode
  N12: R9.Pin_0, LED9.cathode
  N13: R8.Pin_0, LED8.cathode
  N14: R7.Pin_0, LED7.cathode
  N15: R6.Pin_0, LED6.cathode
  N16: R5.Pin_0, LED5.cathode
  N17: R3.Pin_0, LED3.cathode
  N18: R4.Pin_0, LED4.cathode
  N19: R2.Pin_0, LED2.cathode
  N20: R1.Pin_0, LED1.cathode
  N21: LED0.cathode, R0.Pin_0
