# Fritzing sketch Resistor-Value-Calculation (saved by Fritzing 0.9.3b)
breadboards: 1

parts:
  R0 = Resistor [tolerance=±5% resistance=150 package=THT]
  LED0 = LED - 5mm [color="Red (633nm)" package="5 mm [THT]"]

nets:
  N1: R0.Pin_0, LED0.cathode
  GND: R0.Pin_1
